# Fritzing sketch blinking_led (saved by Fritzing 0.9.3b)
breadboards: 1

parts:
  LED1 = LED - 3mm [color="Red (633nm)" package="3 mm [THT]"]
  Part1 = Arduino Uno (Rev3) - ICSP
  R2 = Resistor [tolerance=±5% resistance=220 package="1206 [SMD]"]

nets:
  N1: LED1.cathode, R2.Pin_0
  N2: LED1.anode, Part1.D7
  N3: Part1.GND, R2.Pin_1
